# Fritzing sketch circuit (saved by Fritzing 1.0.6)
breadboards: 1

parts:
  Part1 = Adafruit Trinket M0 [part_number="Adafruit #3500"]
  S1 = Pushbutton [package="[THT]"]
  Part2 = Triple Axis Accelerometer Breakout - ADXL335
  LED1 = smd LED [color="Red (633nm)" package="0603 [SMD]"]
  SG1 = Buzzer 12mm [package=buzzer-ccv-kit]
  R1 = Resistor [tolerance=±5% power=0.25W resistance=220 package=THT]
  Q1 = Basic FET N-Channel [package="D2Pak [SMD]"]
  R2 = Resistor [tolerance=±5% power=0.25W resistance=4.7k package=THT]
  D1 = Schottky Diode [part_number=1N5817 package="Melf DO-213 AB [SMD]"]
  M1 = DC Motor [voltage_(max)=6V voltage_(min)=3V]

nets:
  GND: Part1.GND, S1.Pin_3, S1.Pin_4, Part2.GND, LED1.cathode, SG1.2, Q1.source
  N1: Part1.D3_A3_PA07_RXD_SCK, Part2.ZOUT
  3.3V: Part1.3.3V, Part2.VCC
  N2: Part1.D2_A1_PA09_SCL_MISO, R2.Pin_1
  N3: Part1.D1_A0_PA02, SG1.1, R1.Pin_1
  N4: Part1.D0_A4_PA08_SDA, S1.Pin_1, S1.Pin_2
  N5: Part1.VBUS, D1.cathode, M1.pin_1
  N6: LED1.anode, R1.Pin_0
  N7: Q1.Gate, R2.Pin_0
  N8: Q1.drain, D1.anode, M1.pin_2
