# Fritzing sketch breadboard (saved by Fritzing 1.0.6)
breadboards: 1

parts:
  Part2 = Adafruit ItsyBitsy M4 [part_number="Adafruit #3800"]
  S1 = Momentary Switch [package=ksa_sealed_tac_switch]
  S2 = Momentary Switch [package=ksa_sealed_tac_switch]
  S3 = Momentary Switch [package=ksa_sealed_tac_switch]
  S4 = Momentary Switch [package=ksa_sealed_tac_switch]
  LED1 = smd LED [color="Red (633nm)" package="0805 [SMD]"]
  R1 = Resistor [tolerance=±5% resistance=220 package="1206 [SMD]"]

nets:
  N1: Part2.GND, S1.4, S2.4, S3.4, S4.4, LED1.cathode
  N2: Part2.D12, S1.1
  N3: Part2.D11, S2.1
  N4: Part2.D10, S3.1
  N5: Part2.D9, S4.1
  N6: Part2.D7, R1.Pin_0
  N7: LED1.anode, R1.Pin_1

custom parts:
  Adafruit ItsyBitsy M4: What's smaller than a Feather but larger than a Trinket? It's an Adafruit ItsyBitsy M4 Express featuring the Microchip ATSAMD51! Small, powerful, with a ultra fast ATSAMD51 Cortex M4 processor running at 120 MHz - this microcontroller board is perfect when you want something very compact, with a ton of horsepower and a bunch of pins. This Itsy is like a bullet train, with it's 120MHz Cortex M4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
